// Logisim project Ctl_Shift_Add_Sub_Mov.circ as structural Verilog: 3 circuits, main circuit Shift_Add_Sub_Mov
module Shift_Add_Sub_Mov (
  input  Enable,
  input  [15:0] Instruction,
  output [3:0] Flags_Update_Mask,
  output Carry,
  output Imm32_Enable,
  output [2:0] Rm,
  output [2:0] Rn,
  output [2:0] Rd,
  output [4:0] Imm5,
  output [31:0] Imm32,
  output [3:0] ALU_Opcode
);

  wire bitselector_8_out, Cmp_Add_Imm8, Cmp_Codop, Codop, comparator_9_eq, comparator_10_eq,
       comparator_11_eq, comparator_12_eq, comparator_13_eq, Mov_Cmp_Imm8_Codop_Bool, Move_Codop, not_1_out,
       Only_Add_Codop, Only_Add_Imm3_Codop, Only_Add_Imm8_Codop, Only_Shift_Codop, Shift_Add_Codop,
       Shift_Add_Sub_Codop_Bool;
  wire [1:0] bit_extender_10_out;
  wire [2:0] bit_extender_2_out, bit_extender_3_out, bit_extender_6_out, bit_extender_7_out,
       bit_extender_8_out, bit_extender_13_out, bit_extender_14_out, bit_extender_15_out,
       bit_extender_22_out, bit_extender_23_out, bitselector_17_out, Move_Rd_Out, Only_Shift_Rm_Out,
       Rd_Move_In, Rd_Shift_In, Rm_Add_In, Rm_Shift_In, Rn_Add_In, Shift_Rd_Out;
  wire [3:0] bit_extender_9_out;
  wire [4:0] ALU_Opcode_t, bit_extender_11_out, Imm5_Shift_In;
  wire [5:0] bitselector_12_out;
  wire [7:0] and_7_out, bit_extender_17_out, bit_extender_18_out, bit_extender_19_out, bitselector_2_out,
       Imm3_Add_In, Imm3_Valid, Imm8_In, Imm8_Valid, or_3_out;
  wire [8:0] bitselector_3_out;
  wire [9:0] bitselector_10_out;
  wire [10:0] bitselector_9_out, bitselector_13_out, bitselector_14_out, bitselector_15_out,
       bitselector_18_out, bitselector_19_out;
  wire [11:0] bitselector_11_out;
  wire [15:0] bit_extender_1_out, Instruction_t;
  wire [31:0] bit_extender_16_out, bit_extender_21_out, Mov_Imm8_Valid;

  assign bit_extender_1_out = {{15{Enable}}, Enable};  // Bit_Extender bit_extender_1
  assign Instruction_t = bit_extender_1_out & Instruction;  // AND_Gate and_1, 16 bits wide
  BitSelector #(.group(3), .width(16)) bitselector_1 (.in(Instruction_t), .out(Rd_Shift_In), .sel(3'b000));
  BitSelector #(.group(8), .width(16)) bitselector_2 (.in(Instruction_t), .out(bitselector_2_out), .sel(1'b1));
  assign Rd = Shift_Rd_Out | Move_Rd_Out;  // OR_Gate or_1, 3 bits wide
  assign bit_extender_2_out = {{2{Shift_Add_Codop}}, Shift_Add_Codop};  // Bit_Extender bit_extender_2
  assign Shift_Rd_Out = bit_extender_2_out & Rd_Shift_In;  // AND_Gate and_2, 3 bits wide
  assign bit_extender_3_out = {{2{Move_Codop}}, Move_Codop};  // Bit_Extender bit_extender_3
  assign Move_Rd_Out = bit_extender_3_out & Rd_Move_In;  // AND_Gate and_3, 3 bits wide
  Bit_Extender #(.out_width(3)) bit_extender_4 (.in(bitselector_2_out), .out(Rd_Move_In));
  BitSelector #(.group(9), .width(16)) bitselector_3 (.in(Instruction_t), .out(bitselector_3_out), .sel(1'b1));
  BitSelector #(.width(16)) bitselector_4 (.in(Instruction_t), .out(Codop), .sel(4'b1101));
  Bit_Extender #(.in_width(9), .out_width(5)) bit_extender_5 (.in(bitselector_3_out), .out(ALU_Opcode_t));
  assign bit_extender_6_out = {{2{Only_Add_Codop}}, Only_Add_Codop};  // Bit_Extender bit_extender_6
  not not_1 (not_1_out, Only_Add_Codop);
  assign Rm = bit_extender_6_out & Rm_Add_In;  // AND_Gate and_4, 3 bits wide
  assign bit_extender_7_out = {{2{not_1_out}}, not_1_out};  // Bit_Extender bit_extender_7
  assign Only_Shift_Rm_Out = bit_extender_7_out & Rm_Shift_In;  // AND_Gate and_5, 3 bits wide
  BitSelector #(.group(3), .width(16)) bitselector_5 (.in(Instruction_t), .out(Rm_Shift_In), .sel(3'b001));
  BitSelector #(.group(3), .width(16)) bitselector_6 (.in(Instruction_t), .out(Rm_Add_In), .sel(3'b010));
  Comparator #(.width(1)) comparator_1 (.a(Codop), .b(1'b0), .eq(Shift_Add_Sub_Codop_Bool));  // open: gt, lt
  Comparator #(.width(1)) comparator_2 (.a(Codop), .b(1'b1), .eq(Mov_Cmp_Imm8_Codop_Bool));  // open: gt, lt
  ALU_Opcode_Calculator alu_opcode_calculator_1 (.AluOpcode(ALU_Opcode_t), .Codop(ALU_Opcode));
  Flag_Calculator flag_calculator_1 (.AluOpcode(ALU_Opcode), .Flag(Flags_Update_Mask));
  assign Rn = Only_Shift_Rm_Out | Rn_Add_In;  // OR_Gate or_2, 3 bits wide
  BitSelector #(.group(3), .width(16)) bitselector_7 (.in(Instruction_t), .out(Rn_Add_In), .sel(3'b001));
  BitSelector #(.width(16)) bitselector_8 (.in(Instruction_t), .out(bitselector_8_out), .sel(4'b1101));
  Bit_Extender #(.in_width(11), .out_width(3)) bit_extender_8 (.in(bitselector_9_out), .out(bit_extender_8_out));
  BitSelector #(.group(11), .width(16)) bitselector_9 (.in(Instruction_t), .out(bitselector_9_out), .sel(1'b1));
  Bit_Extender #(.in_width(10), .out_width(4)) bit_extender_9 (.in(bitselector_10_out), .out(bit_extender_9_out));
  BitSelector #(.group(10), .width(16)) bitselector_10 (.in(Instruction_t), .out(bitselector_10_out), .sel(1'b1));
  Bit_Extender #(.in_width(12), .out_width(2)) bit_extender_10 (.in(bitselector_11_out), .out(bit_extender_10_out));
  BitSelector #(.group(12), .width(16)) bitselector_11 (.in(Instruction_t), .out(bitselector_11_out), .sel(1'b1));
  Comparator #(.width(1)) comparator_3 (.a(bitselector_8_out), .b(1'b0), .eq(Shift_Add_Codop));  // open: gt, lt
  Comparator #(.width(4)) comparator_4 (.a(ALU_Opcode), .b(4'b1001), .eq(Move_Codop));  // open: gt, lt
  Comparator #(.width(4)) comparator_5 (.a(ALU_Opcode), .b(4'b1010), .eq(Cmp_Codop));  // open: gt, lt
  Comparator #(.width(3)) comparator_6 (.a(bit_extender_8_out), .b(3'b011), .eq(Only_Add_Codop));  // open: gt, lt
  Comparator #(.width(4)) comparator_7 (.a(bit_extender_9_out), .b(4'b0111), .eq(Only_Add_Imm3_Codop));  // open: gt, lt
  Comparator #(.width(2)) comparator_8 (.a(bit_extender_10_out), .b(2'b11), .eq(Only_Add_Imm8_Codop));  // open: gt, lt
  assign bit_extender_11_out = {{4{Only_Shift_Codop}}, Only_Shift_Codop};  // Bit_Extender bit_extender_11
  assign Imm5 = bit_extender_11_out & Imm5_Shift_In;  // AND_Gate and_6, 5 bits wide
  BitSelector #(.group(6), .width(16)) bitselector_12 (.in(Instruction_t), .out(bitselector_12_out), .sel(2'b01));
  Bit_Extender #(.in_width(6), .out_width(5)) bit_extender_12 (.in(bitselector_12_out), .out(Imm5_Shift_In));
  BitSelector #(.group(11), .width(16)) bitselector_13 (.in(Instruction_t), .out(bitselector_13_out), .sel(1'b1));
  BitSelector #(.group(11), .width(16)) bitselector_14 (.in(Instruction_t), .out(bitselector_14_out), .sel(1'b1));
  BitSelector #(.group(11), .width(16)) bitselector_15 (.in(Instruction_t), .out(bitselector_15_out), .sel(1'b1));
  assign or_3_out = Imm8_Valid | Imm3_Valid;  // OR_Gate or_3, 8 bits wide
  Bit_Extender #(.in_width(11), .out_width(3)) bit_extender_13 (.in(bitselector_13_out), .out(bit_extender_13_out));
  Bit_Extender #(.in_width(11), .out_width(3)) bit_extender_14 (.in(bitselector_14_out), .out(bit_extender_14_out));
  Bit_Extender #(.in_width(11), .out_width(3)) bit_extender_15 (.in(bitselector_15_out), .out(bit_extender_15_out));
  assign bit_extender_16_out = {{24{1'b0}}, or_3_out};  // Bit_Extender bit_extender_16
  Comparator #(.width(3)) comparator_9 (.a(bit_extender_13_out), .b(3'b000), .eq(comparator_9_eq));  // open: gt, lt
  Comparator #(.width(3)) comparator_10 (.a(bit_extender_14_out), .b(3'b001), .eq(comparator_10_eq));  // open: gt, lt
  Comparator #(.width(3)) comparator_11 (.a(bit_extender_15_out), .b(3'b010), .eq(comparator_11_eq));  // open: gt, lt
  assign Imm32 = bit_extender_16_out | Mov_Imm8_Valid;  // OR_Gate or_4, 32 bits wide
  or or_5 (Only_Shift_Codop, comparator_9_eq, comparator_10_eq, comparator_11_eq);
  assign bit_extender_17_out = {{7{Move_Codop}}, Move_Codop};  // Bit_Extender bit_extender_17
  assign bit_extender_18_out = {{7{Cmp_Add_Imm8}}, Cmp_Add_Imm8};  // Bit_Extender bit_extender_18
  assign bit_extender_19_out = {{7{Only_Add_Imm3_Codop}}, Only_Add_Imm3_Codop};  // Bit_Extender bit_extender_19
  BitSelector #(.group(8), .width(16)) bitselector_16 (.in(Instruction_t), .out(Imm8_In), .sel(1'b0));
  BitSelector #(.group(3), .width(16)) bitselector_17 (.in(Instruction_t), .out(bitselector_17_out), .sel(3'b000));
  assign and_7_out = bit_extender_17_out & Imm8_In;  // AND_Gate and_7, 8 bits wide
  assign Imm8_Valid = bit_extender_18_out & Imm8_In;  // AND_Gate and_8, 8 bits wide
  assign Imm3_Valid = bit_extender_19_out & Imm3_Add_In;  // AND_Gate and_9, 8 bits wide
  assign Imm3_Add_In = {{5{1'b0}}, bitselector_17_out};  // Bit_Extender bit_extender_20
  assign bit_extender_21_out = {{24{1'b0}}, and_7_out};  // Bit_Extender bit_extender_21
  Negator #(.width(32)) negator_1 (.in(bit_extender_21_out), .out(Mov_Imm8_Valid));
  or or_6 (Cmp_Add_Imm8, Cmp_Codop, Only_Add_Imm8_Codop);
  BitSelector #(.group(11), .width(16)) bitselector_18 (.in(Instruction_t), .out(bitselector_18_out), .sel(1'b1));
  BitSelector #(.group(11), .width(16)) bitselector_19 (.in(Instruction_t), .out(bitselector_19_out), .sel(1'b1));
  Bit_Extender #(.in_width(11), .out_width(3)) bit_extender_22 (.in(bitselector_18_out), .out(bit_extender_22_out));
  Bit_Extender #(.in_width(11), .out_width(3)) bit_extender_23 (.in(bitselector_19_out), .out(bit_extender_23_out));
  Comparator #(.width(3)) comparator_12 (.a(bit_extender_22_out), .b(3'b110), .eq(comparator_12_eq));  // open: gt, lt
  Comparator #(.width(3)) comparator_13 (.a(bit_extender_23_out), .b(3'b111), .eq(comparator_13_eq));  // open: gt, lt
  or or_7 (Only_Add_Imm8_Codop, comparator_12_eq, comparator_13_eq);
  or or_8 (Imm32_Enable, Cmp_Add_Imm8, Move_Codop, Only_Add_Imm3_Codop);
  or or_9 (Carry, Shift_Add_Codop, Cmp_Codop, Only_Add_Imm3_Codop, Only_Add_Imm8_Codop);

  // Other names for the same wires on the sheet: Carry_enable = Carry; Flag_Out[3:0] = Flags_Update_Mask;
  //   Imm32_Out[31:0] = Imm32; Imm5_Out[4:0] = Imm5; Only_Shift_imm5_Out[4:0] = Imm5; Opcode[3:0] = ALU_Opcode;
  //   Rd_Out[2:0] = Rd; Only_Add_Rm_Out[2:0] = Rm; Rm_Out[2:0] = Rm; Rn_Out[2:0] = Rn

  // Notes on the sheet:
  //   Note: ALU uses Rn register for shifts. Use Rn instead of Rm for shifts (immediate) here too
  //   Note 3: Imm32_Enable forces the use of the immediate for Rm register
  //   Note 2: MOV uses RSB ALU opcode with Imm8 reversed so that it is copied to output register
  //   Pull output low on Enable = 0
  //   only ADD and SUB use Rm
  //   Enable carry for SUB since it is reversed in ALU
  //   ALU will use Imm32 instead of Rm
endmodule

module ALU_Opcode_Calculator (
  input  [4:0] AluOpcode,
  output [3:0] Codop
);

  wire and_2_out, and_3_out, and_4_out, and_5_out, and_6_out, and_7_out, not_1_out, not_2_out, not_3_out,
       not_4_out;

  not not_1 (not_1_out, AluOpcode[4]);
  not not_2 (not_2_out, AluOpcode[3]);
  not not_3 (not_3_out, AluOpcode[2]);
  not not_4 (not_4_out, AluOpcode[0]);
  and and_1 (Codop[3], AluOpcode[4], not_2_out);
  and and_2 (and_2_out, not_1_out, not_2_out);
  and and_3 (and_3_out, AluOpcode[2], AluOpcode[0]);
  and and_4 (and_4_out, AluOpcode[4], AluOpcode[2]);
  and and_5 (and_5_out, not_1_out, not_2_out, AluOpcode[2]);
  and and_6 (and_6_out, not_1_out, AluOpcode[2], not_4_out);
  and and_7 (and_7_out, AluOpcode[4], not_3_out);
  or or_1 (Codop[1], and_2_out, and_3_out, and_4_out);
  or or_2 (Codop[0], and_5_out, and_6_out, and_7_out);

  assign Codop[2] = AluOpcode[3];
endmodule

module Flag_Calculator (
  input  [3:0] AluOpcode,
  output [3:0] Flag
);

  wire comparator_1_eq, comparator_2_eq, comparator_3_eq, comparator_4_eq;

  not not_1 (Flag[1], comparator_1_eq);
  Comparator #(.width(4)) comparator_1 (.a(AluOpcode), .b(4'b1001), .eq(comparator_1_eq));  // open: gt, lt
  Comparator #(.width(4)) comparator_2 (.a(AluOpcode), .b(4'b1010), .eq(comparator_2_eq));  // open: gt, lt
  Comparator #(.width(4)) comparator_3 (.a(AluOpcode), .b(4'b0101), .eq(comparator_3_eq));  // open: gt, lt
  Comparator #(.width(4)) comparator_4 (.a(AluOpcode), .b(4'b0110), .eq(comparator_4_eq));  // open: gt, lt
  or or_1 (Flag[0], comparator_2_eq, comparator_3_eq, comparator_4_eq);

  assign Flag[3:2] = 2'b11;

  // Other names for the same wires on the sheet: V_Flag = Flag[0]; C_Flag = Flag[1]; Opcode[3:0] = AluOpcode
endmodule
